# Fritzing sketch schema (saved by Fritzing 0.9.4)
breadboards: 1

parts:
  HC-SR04_Sensor_1 = HC-SR04 Ultrasonic Distance Sensor
  LED1 = LED - 5mm [color="Red (633nm)" package="5 mm [THT]"]
  LED2 = LED - 5mm [color="Green (570nm)" package="5 mm [THT]"]
  R1 = Resistor [tolerance=±5% resistance=220 package="0603 [SMD]"]
  R2 = Resistor [tolerance=±5% resistance=220 package="0603 [SMD]"]
  U1 = ESP8266 WiFi Module [part_number=ESP8266]
  VCC1 = 4 x AAA Battery Mount

nets:
  N1: HC-SR04_Sensor_1.VCC, VCC1.+
  N2: HC-SR04_Sensor_1.TRIG, U1.D0
  N3: HC-SR04_Sensor_1.ECHO, U1.D1
  N4: HC-SR04_Sensor_1.GND, LED1.cathode, LED2.cathode, R2.Pin_1, U1.D2, VCC1.-
  N5: LED1.anode, R1.Pin_0
  N6: LED2.anode, R2.Pin_0
  N7: R1.Pin_1, U1.D3
